// Logisim project ALU.circ as structural Verilog: 1 circuit, main circuit main
module main (
  input  OPCODE_0,
  input  OPCODE_1,
  input  OPCODE_2,
  input  ALT_OPCODE,
  input  INPUT0_0,
  input  INPUT0_1,
  input  INPUT0_2,
  input  INPUT0_3,
  input  INPUT1_0,
  input  INPUT1_1,
  input  INPUT1_2,
  input  INPUT1_3,
  output OUTPUT0_0,
  output OUTPUT0_1,
  output OUTPUT0_2,
  output OUTPUT0_3,
  output OUTPUT1_0,
  output OUTPUT1_1,
  output OUTPUT1_2,
  output OUTPUT1_3,
  output CARRY,
  output NEGATIVE,
  output OVERFLOW,
  output ZERO
);
endmodule
